# Fritzing sketch arduino-shield (saved by Fritzing 0.9.3b)
circuit board: 8.46667cm x 5.64444cm
breadboards: 1

parts:
  Part1 = Arduino Uno (Rev3)
  R1 = Resistor [tolerance=±5% resistance=4.7k package="0805 [SMD]"]
  R2 = Resistor [tolerance=±5% resistance=4.7k package="0805 [SMD]"]
  SDA = Header 1 [package=snap-male]
  GND = Header 1 [package=snap-male]
  SCL = Header 1 [package=snap-male]
  3_3V = Header 1 [package=snap-male]
  5V = Header 1 [package=snap-male]

nets:
  N1: Part1.A4/SDA, R2.Pin_1, SDA.1
  N2: Part1.A5/SCL, R1.Pin_1, SCL.1
  N3: Part1.3V3, 3_3V.1
  N4: Part1.5V, R1.Pin_0, R2.Pin_0, 5V.1
  N5: Part1.GND, GND.1
